# Fritzing sketch circit (saved by Fritzing 0.9.3b)
perfboards: 1

parts:
  Mod1 = Raspberry Pi 4B
  U1 = ESP32-38PinWide [part_number=ESP32-38PinWide]
  J1 = Power Jack [package=power_jack_smd]
  Buck_Convertor1 = Buck Convertor [part_number=LM2596 package=THT]
  RGB_Strip_LED1 = RGB Strip LED
  U3 = 2-Channel 5v Relay Shield [package=relay-2ch5v10a]
  M1 = DC Motor
  Q2 = Basic FET P-Channel [package="TO220 [THT]"]
  Q4 = Basic FET P-Channel [package="TO220 [THT]"]
  Q3 = Basic FET P-Channel [package="TO220 [THT]"]
  R8 = Resistor [tolerance=±5% resistance=220 package="0805 [SMD]"]
  R7 = Resistor [tolerance=±5% resistance=220 package="0805 [SMD]"]
  R4 = Resistor [tolerance=±5% resistance=220 package="0805 [SMD]"]
  Q1 = Basic FET N-Channel [package="D2Pak [SMD]"]
  R5 = Resistor [tolerance=±5% resistance=220 package="0805 [SMD]"]
  R2 = Resistor [tolerance=±5% resistance=220 package="0805 [SMD]"]  # not connected
  R1 = Resistor [tolerance=±5% resistance=220 package="0805 [SMD]"]
  R3 = Resistor [tolerance=±5% resistance=220 package=THT]
  R6 = Resistor [tolerance=±5% resistance=220 package="0805 [SMD]"]
  J2 = Basic Servo

nets:
  5V: Mod1.5V, Buck_Convertor1.Positive_Output, U3.VCC
  GND: Mod1.GND, Buck_Convertor1.Negative_Output, U3.GND, M1.pin_1
  N1: Mod1.GPIO14, U1.GPIO3
  N2: Mod1.GPIO15, U1.GPIO1
  N3: U1.GPIO19, J2.pulse
  N4: J1.PWR, Buck_Convertor1.Positive_Input
  N5: J1.GND, Buck_Convertor1.Negative_Input, RGB_Strip_LED1.Blue_Connect#5, U3.K1-In, U3.K2-In, Q2.drain, Q4.drain, Q3.drain, R4.Pin_1, Q1.drain, R5.Pin_1, R6.Pin_1
  N6: RGB_Strip_LED1.Common_Connect#4, U3.K2-On
  N7: U3.K1-Off, M1.pin_2
  N8: Q4.gate, R8.Pin_0, R7.Pin_1
  N9: Q3.gate, R3.Pin_1, R6.Pin_0
  N10: R4.Pin_0, Q1.Gate, R1.Pin_1

notes:
  Pinouts
  =================
  - Led
  - Pneumatic pin relay
  - Motor
  - Ejector 1,2,3,4
  To ejector valve 1
  To ejector valve 2
  To ejector valve 3
  To ejector valve 4
  ESP32
  raspberry Pi 4
  Vibration Motor
  White LED
  2 Channel relay

custom parts:
  ESP32-38PinWide: Generic 38-Pin ESP32 with wide format (only access to one side of pins on a breadboard) based on Stephen Lilley's HiLetgo ESP-WROOM-32 ESP32 ESP-32S Development Board.
  Buck Convertor: DC to DC buck convertor
  RGB Strip LED: A tri-color Strip LED with red, green and blue. Pin order: red - common cathode - blue - green
  2-Channel 5v Relay Shield: 2 Channel 5v Relay Shield w. 2x SPD-06VDC-SD-C
